# Fritzing sketch audio-detector (saved by Fritzing 0.9.4)
breadboards: 1

parts:
  Part1 = Arduino Nano (Rev3.0) (ICSP)
  LED1 = LED - 5mm [color="Red (633nm)" package="5 mm [THT]"]
  LED2 = smd LED [color="Red (633nm)" package="0603 [SMD]"]
  R1 = Resistor [tolerance=±5% resistance=220 package="0603 [SMD]"]
  R2 = Resistor [tolerance=±5% resistance=220 package="0603 [SMD]"]
  S1 = Momentary Switch [package=tactile-pth]
  IR1 = TSOP312.., 314.. [package=THT]
  LED3 = smd LED [color="Infrared (940nm)" package="0805 [SMD]"]
  R3 = Resistor [tolerance=±5% resistance=100 package="0603 [SMD]"]  # not connected

nets:
  GND: Part1.GND, R1.Pin_0, R2.Pin_0, S1.1, IR1.GND
  N1: Part1.D3, LED3.anode
  N2: Part1.D10, S1.4
  N3: Part1.D11/MOSI, IR1.Data
  N4: Part1.D12/MISO, LED2.anode
  N5: Part1.5V, IR1.Vs
  N6: Part1.D13/SCK, LED1.anode
  N7: LED1.cathode, R1.Pin_1
  N8: LED2.cathode, R2.Pin_1

notes:
  IR receiver, HW-447
  code stored LED, indicates when IR code was saved in EEPROM
  status LED, indicates when the code is sent
  button sends the IR code over PWM3 pin
  IR LED for sending of the recorded code
